# Fritzing sketch SmartScaletainer (saved by Fritzing 0.9.4)
breadboards: 1

parts:
  Argon1 = Particle Argon
  Part1 = BME280 Breakout  # not connected
  OLED_I2C1 = OLED 128x64 I2C Monochrome Display
  OLED_I2C2 = OLED 128x64 I2C Monochrome Display
  Part2 = KY-003 Hall Magnetic Sensor Module [package="Breakout board"]  # not connected
  Load_Cell1 = Load Cell - Red/white/black/green
  Load_Cell2 = Load Cell - Red/white/black/green
  Part4 = HX711 Weighing Sensor Module
  Part5 = HX711 Weighing Sensor Module

nets:
  VDD: Argon1.3.3V, OLED_I2C1.VDD, OLED_I2C2.VDD, Part5.VCC
  GND: Argon1.GND, OLED_I2C1.GND, OLED_I2C2.GND, Part5.GND
  N1: Argon1.SDA, OLED_I2C1.SDA, OLED_I2C2.SDA
  N2: Argon1.SCL, OLED_I2C1.SCK, OLED_I2C2.SCK
  N3: Argon1.D6, Part5.DO/RX
  N4: Argon1.D7, Part5.CK/TX
  N5: Load_Cell1.wire1, Part4.E+
  N6: Load_Cell1.wire2, Part4.A-
  N7: Load_Cell1.wire3, Part4.E-
  N8: Load_Cell1.wire4, Part4.A+
  N9: Load_Cell2.wire1, Part5.E+
  N10: Load_Cell2.wire2, Part5.A-
  N11: Load_Cell2.wire3, Part5.E-
  N12: Load_Cell2.wire4, Part5.A+

custom parts:
  Particle Argon: The Argon is a powerful Wi-Fi enabled development board that can act as either a standalone Wi-Fi endpoint or Wi-Fi enabled gateway for Particle Mesh networks. It is based on the Nordic nRF52840 and has built-in battery charging circuitry so it’s easy to connect a Li-Po and deploy your local network in minutes. The Argon is great for connecting existing projects to the Particle Device Cloud or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
  KY-003 Hall Magnetic Sensor Module: KEYES KY-003 Arduino Hall Magnetic Sensor Module is a switch that will turn on/off in the presence of a magnetic field.
  Load Cell - Red/white/black/green: A rectangle load cell/weighting pressure Sensor with four wires - Red, white, black, green. Normally corresponding with E+, E-, A+, A- respectively.
